// Digital circuit 3.1.circuit.dig as structural Verilog
module _3_1_circuit (
  input  x0,
  input  x1,
  output y0
);

  wire and_1_out, nor_1_out, nor_2_out, not_1_out, or_1_out;

  not not_1 (not_1_out, x1);
  nor nor_1 (nor_1_out, x0, not_1_out);
  and and_1 (and_1_out, x1, x0);
  or or_1 (or_1_out, x1, x0);
  nor nor_2 (nor_2_out, nor_1_out, and_1_out);
  nand nand_1 (y0, nor_2_out, or_1_out);
endmodule
