// Digital circuit 3.2.circuit.dig as structural Verilog
module _3_2_circuit (
  input  x1,
  input  x0,
  output y0
);

  wire not_1_out;

  not not_1 (not_1_out, x0);
  or or_1 (y0, not_1_out, x1);
endmodule
