// Digital circuit 4.3.circuit.dig as structural Verilog
module _4_3_circuit (
  input  x0,
  input  x1,
  input  x2,
  output y0
);

  wire and_1_out, and_2_out, and_3_out, not_1_out, xor_1_out;

  not not_1 (not_1_out, x0);
  xor xor_1 (xor_1_out, x1, x2);
  and and_1 (and_1_out, x1, x2);
  and and_2 (and_2_out, xor_1_out, x0);
  and and_3 (and_3_out, and_1_out, not_1_out);
  or or_1 (y0, and_2_out, and_3_out);
endmodule
