// Digital circuit 1a_circuit.dig as structural Verilog
module _1a_circuit (
  input  x0,
  input  x1,
  input  x2,
  input  x3,
  input  x4,
  output y0
);

  wire and_1_out, or_1_out, or_2_out;

  or or_1 (or_1_out, ~x1, ~x2);  // Or
  or or_2 (or_2_out, ~x3, ~x4);  // Or
  and and_1 (and_1_out, or_1_out, or_2_out);
  or or_3 (y0, ~x0, and_1_out);  // Or
endmodule
