// Digital circuit 1b_circuit.dig as structural Verilog
module _1b_circuit (
  input  x0,
  input  x1,
  input  x2,
  input  x3,
  input  x4,
  input  x5,
  input  x6,
  output y0
);

  wire and_1_out, and_2_out, or_1_out, or_2_out;

  or or_1 (or_1_out, ~x1, ~x2);  // Or
  and and_1 (and_1_out, x3, x4, x5);
  and and_2 (and_2_out, ~x0, or_1_out);  // And
  or or_2 (or_2_out, and_1_out, ~x6);  // Or
  or or_3 (y0, and_2_out, or_2_out);
endmodule
