// Digital circuit 2d_f_circuit.dig as structural Verilog
module _2d_f_circuit (
  input  x0,
  input  x1,
  input  x2,
  output f
);

  wire and_1_out, nor_1_out, not_1_out;

  not not_1 (not_1_out, x2);
  nor nor_1 (nor_1_out, x0, x1);
  and and_1 (and_1_out, x0, x1);
  or or_1 (f, nor_1_out, not_1_out, and_1_out);
endmodule
