// Digital circuit 2d_g_circuit.dig as structural Verilog
module _2d_g_circuit (
  input  x0,
  input  x1,
  input  x2,
  input  x3,
  output g
);

  wire or_1_out, or_2_out;

  or or_1 (or_1_out, x1, x2);
  or or_2 (or_2_out, x2, x3);
  nand nand_1 (g, or_1_out, or_2_out);
endmodule
