// Digital circuit 1c_4to1_MUX.dig as structural Verilog
module _1c_4to1_MUX (
  input  x0,
  input  [1:0] s2_1,
  input  x1,
  output y0
);

  Multiplexer #(.Selector_Bits(2)) multiplexer_1 (.sel(s2_1), .in_0(x0), .in_1(x1), .in_2(x1), .in_3(x0), .out(y0));
endmodule
