// Digital circuit 2c2d_4bitRipple-Carry-Adder_withTB.dig as structural Verilog
module _2c2d_4bitRipple_Carry_Adder_withTB (
  input  A_0,
  input  B_0,
  input  C_in,
  input  A_1,
  input  B_1,
  input  B_2,
  input  A_2,
  input  A_3,
  input  B_3,
  output C_out,
  output S_0,
  output S_1,
  output S_2,
  output S_3
);

  wire _2b_full_adder_1_c_i, _2b_full_adder_2_c_i, _2b_full_adder_3_c_i;

  _2b_Full_Adder _2b_full_adder_1 (.A_i(A_0), .B_i(B_0), .C_i_1(C_in), .S_i(S_0), .C_i(_2b_full_adder_1_c_i));
  _2b_Full_Adder _2b_full_adder_2 (
    .A_i(A_1), .B_i(B_1), .C_i_1(_2b_full_adder_1_c_i), .S_i(S_1), .C_i(_2b_full_adder_2_c_i));
  _2b_Full_Adder _2b_full_adder_3 (
    .A_i(A_2), .B_i(B_2), .C_i_1(_2b_full_adder_2_c_i), .S_i(S_2), .C_i(_2b_full_adder_3_c_i));
  _2b_Full_Adder _2b_full_adder_4 (.A_i(A_3), .B_i(B_3), .C_i_1(_2b_full_adder_3_c_i), .S_i(S_3), .C_i(C_out));
endmodule

/* Test case 2d TestBench:
A_3 A_2 A_1 A_0 B_3 B_2 B_1 B_0 C_out S_3 S_2 S_1 S_0  
0 0 0 0 0 0 0 0 0 0 0 0 0 
0 0 0 0 1 0 0 0 0 1 0 0 0
0 0 1 1 0 1 1 1 0 1 0 1 0
1 0 1 1 0 1 1 0 1 0 0 0 1
1 1 1 1 0 0 0 1 1 0 0 0 0
1 1 1 1 1 1 1 1 1 1 1 1 0
*/
