// Digital circuit 3a_2erComplement_circuit.dig as structural Verilog
module _3a_2erComplement_circuit (
  input  A_0,
  input  A_1,
  input  A_2,
  input  A_3,
  input  C_in,
  output S_0,
  output C_out,
  output S_1,
  output S_2,
  output S_3
);

  wire not_1_out, not_2_out, not_3_out, not_4_out;

  not not_1 (not_1_out, A_0);
  not not_2 (not_2_out, A_1);
  not not_3 (not_3_out, A_2);
  not not_4 (not_4_out, A_3);
  _2c2d_4bitRipple_Carry_Adder_withTB _2c2d_4bitripple_carry_adder_withtb_1 (
    .A_0(not_1_out), .B_0(1'b1), .C_in(C_in), .A_1(not_2_out), .B_1(1'b0), .B_2(1'b0), .A_2(not_3_out),
    .A_3(not_4_out), .B_3(1'b0), .C_out(C_out), .S_0(S_0), .S_1(S_1), .S_2(S_2), .S_3(S_3));
endmodule
