// Digital circuit 3cd_Subtraction_circuit.dig as structural Verilog
module _3cd_Subtraction_circuit (
  input  A_0,
  input  A_1,
  input  A_2,
  input  A_3,
  input  C_in,
  input  B_0,
  input  B_1,
  input  B_2,
  input  B_3,
  output C,
  output S_0,
  output S_1,
  output S_2,
  output S_3
);

  wire _2c2d_4bitripple_carry_adder_withtb_1_c_out, _3a_2ercomplement_circuit_1_s_0,
       _3a_2ercomplement_circuit_1_s_1, _3a_2ercomplement_circuit_1_s_2, _3a_2ercomplement_circuit_1_s_3,
       nor_1_out, not_1_out;

  _3a_2erComplement_circuit _3a_2ercomplement_circuit_1 (
    .A_0(A_0), .A_1(A_1), .A_2(A_2), .A_3(A_3), .C_in(C_in), .S_0(_3a_2ercomplement_circuit_1_s_0),
    .S_1(_3a_2ercomplement_circuit_1_s_1), .S_2(_3a_2ercomplement_circuit_1_s_2),
    .S_3(_3a_2ercomplement_circuit_1_s_3));  // open: C_out
  _2c2d_4bitRipple_Carry_Adder_withTB _2c2d_4bitripple_carry_adder_withtb_1 (
    .A_0(_3a_2ercomplement_circuit_1_s_0), .B_0(B_0), .C_in(1'b0), .A_1(_3a_2ercomplement_circuit_1_s_1),
    .B_1(B_1), .B_2(B_2), .A_2(_3a_2ercomplement_circuit_1_s_2), .A_3(_3a_2ercomplement_circuit_1_s_3),
    .B_3(B_3), .C_out(_2c2d_4bitripple_carry_adder_withtb_1_c_out), .S_0(S_0), .S_1(S_1), .S_2(S_2), .S_3(S_3));
  nor nor_1 (nor_1_out, _3a_2ercomplement_circuit_1_s_0, _3a_2ercomplement_circuit_1_s_1, _3a_2ercomplement_circuit_1_s_2, _3a_2ercomplement_circuit_1_s_3);
  not not_1 (not_1_out, _2c2d_4bitripple_carry_adder_withtb_1_c_out);
  xor xor_1 (C, nor_1_out, not_1_out);
endmodule

/* Test case 3d Testbench:
B_3 B_2 B_1 B_0 A_3 A_2 A_1 A_0 C S_3 S_2 S_1 S_0
0 0 0 0  0 0 0 0  0  0 0 0 0
0 0 1 0  0 0 1 0  0  0 0 0 0
0 0 1 0  0 0 1 1  1  1 1 1 1
0 1 0 0  1 0 0 0  1  1 1 0 0
0 1 1 1  1 1 1 1  1  1 0 0 0
1 1 1 1  0 0 0 0  0  1 1 1 1
0 0 0 1  0 0 0 0  0  0 0 0 1
0 1 0 0  0 0 1 0  0  0 0 1 0
*/
