// Digital circuit 1a_2to1_MUX.dig as structural Verilog
module _1a_2to1_MUX (
  input  x_0,
  input  x_1,
  input  S,
  output y_0
);

  wire and_1_out, and_2_out, not_1_out;

  not not_1 (not_1_out, S);
  and and_1 (and_1_out, not_1_out, x_0);
  and and_2 (and_2_out, S, x_1);
  or or_1 (y_0, and_1_out, and_2_out);

  // Notes on the sheet:
  //   Notiz:
  //   Ausgabe x_0, wenn S = 0; 
  //   sonst Ausgabe x_1.
  //   y_0 = (¬S ∧ x_0) ∨ (S ∧ x_1)
endmodule
