// Digital circuit 1b_8to1_MUX.dig as structural Verilog
module _1b_8to1_MUX (
  input  x_7,
  input  x_6,
  input  x_5,
  input  x_4,
  input  x_3,
  input  x_2,
  input  x_1,
  input  x_0,
  input  S_2,
  input  S_1,
  input  S_0,
  output y_0
);

  wire _1a_2to1_mux_1_y_0, _1a_2to1_mux_2_y_0, _1a_2to1_mux_3_y_0, _1a_2to1_mux_4_y_0, _1a_2to1_mux_5_y_0,
       _1a_2to1_mux_6_y_0;

  _1a_2to1_MUX _1a_2to1_mux_1 (.x_0(x_0), .x_1(x_1), .S(S_0), .y_0(_1a_2to1_mux_1_y_0));
  _1a_2to1_MUX _1a_2to1_mux_2 (.x_0(x_2), .x_1(x_3), .S(S_0), .y_0(_1a_2to1_mux_2_y_0));
  _1a_2to1_MUX _1a_2to1_mux_3 (.x_0(x_4), .x_1(x_5), .S(S_0), .y_0(_1a_2to1_mux_3_y_0));
  _1a_2to1_MUX _1a_2to1_mux_4 (.x_0(x_6), .x_1(x_7), .S(S_0), .y_0(_1a_2to1_mux_4_y_0));
  _1a_2to1_MUX _1a_2to1_mux_5 (.x_0(_1a_2to1_mux_1_y_0), .x_1(_1a_2to1_mux_2_y_0), .S(S_1), .y_0(_1a_2to1_mux_5_y_0));
  _1a_2to1_MUX _1a_2to1_mux_6 (.x_0(_1a_2to1_mux_3_y_0), .x_1(_1a_2to1_mux_4_y_0), .S(S_1), .y_0(_1a_2to1_mux_6_y_0));
  _1a_2to1_MUX _1a_2to1_mux_7 (.x_0(_1a_2to1_mux_5_y_0), .x_1(_1a_2to1_mux_6_y_0), .S(S_2), .y_0(y_0));
endmodule
