// Digital circuit 1c_gegOriginal.dig as structural Verilog
module _1c_gegOriginal (
  input  x0,
  input  [2:0] s3_1,
  output y
);

  Multiplexer #(.Selector_Bits(3)) multiplexer_1 (
    .sel(s3_1), .in_0(x0), .in_1(1'b0), .in_2(x0), .in_3(1'b1), .in_4(1'b0), .in_5(x0), .in_6(1'b1),
    .in_7(x0), .out(y));
  // Pins of 1 and 3 bits meet at s3_1
endmodule
