// Digital circuit 2a_Half-Adder.dig as structural Verilog
module _2a_Half_Adder (
  input  A,
  input  B,
  output S,
  output C
);

  wire nand_1_out, nand_2_out, nand_3_out, nand_4_out, nand_5_out, nand_7_out, nand_8_out;

  nand nand_1 (nand_1_out, A, B);
  nand nand_2 (nand_2_out, A, B);
  nand nand_3 (nand_3_out, A, B);
  nand nand_4 (nand_4_out, A, A);
  nand nand_5 (nand_5_out, B, B);
  nand nand_6 (C, nand_1_out, nand_2_out);
  nand nand_7 (nand_7_out, nand_4_out, nand_5_out);
  nand nand_8 (nand_8_out, nand_3_out, nand_7_out);
  nand nand_9 (S, nand_8_out, nand_8_out);
endmodule
