// Digital circuit 2b_Full-Adder.dig as structural Verilog
module _2b_Full_Adder (
  input  A_i,
  input  B_i,
  input  C_i_1,
  output S_i,
  output C_i
);

  wire _2a_half_adder_1_c, _2a_half_adder_1_s, _2a_half_adder_2_c, nand_1_out, nand_2_out;

  _2a_Half_Adder _2a_half_adder_1 (.A(A_i), .B(B_i), .S(_2a_half_adder_1_s), .C(_2a_half_adder_1_c));
  _2a_Half_Adder _2a_half_adder_2 (.A(_2a_half_adder_1_s), .B(C_i_1), .S(S_i), .C(_2a_half_adder_2_c));
  nand nand_1 (nand_1_out, _2a_half_adder_1_c, _2a_half_adder_1_c);
  nand nand_2 (nand_2_out, _2a_half_adder_2_c, _2a_half_adder_2_c);
  nand nand_3 (C_i, nand_1_out, nand_2_out);
endmodule
