// Digital circuit 2ab_4bit_shifter.dig as structural Verilog
module _2ab_4bit_shifter (
  input  a_3,
  input  a_2,
  input  a_1,
  input  a_0,
  input  d,
  output s_3,
  output s_2,
  output s_1,
  output s_0
);

  Multiplexer multiplexer_1 (.sel(d), .in_0(a_1), .in_1(1'b0), .out(s_0));
  Multiplexer multiplexer_2 (.sel(d), .in_0(a_2), .in_1(a_0), .out(s_1));
  Multiplexer multiplexer_3 (.sel(d), .in_0(a_3), .in_1(a_1), .out(s_2));
  Multiplexer multiplexer_4 (.sel(d), .in_0(1'b0), .in_1(a_2), .out(s_3));

  // Notes on the sheet:
  //   4-bit shifter nur mit Multiplexern (2a,b)
  //   L:1  R:0
  //   Notizen:
  //   if d then s_0 := 0.
  //   else      s_0 := a_1.
  //   if d then s_1 := a_0;
  //    else      s_1 := a_2.
  //   if d then s_2 := a_1;
  //    else            s_2 := a_3.
  //   if d then s_3 := a_2;
  //    else            s_3 := 0.
endmodule

/* Test case:
a_3 a_2 a_1 a_0 d s_3 s_2 s_1 s_0
0 0 0 0  0  0 0 0 0
0 0 0 0  1  0 0 0 0
0 0 0 1  0  0 0 0 0
0 0 0 1  1  0 0 1 0
0 0 1 0  0  0 0 0 1
0 0 1 0  1  0 1 0 0
0 0 1 1  0  0 0 0 1
0 0 1 1  1  0 1 1 0
0 1 0 0  0  0 0 1 0
0 1 0 0  1  1 0 0 0
0 1 0 1  0  0 0 1 0
0 1 0 1  1  1 0 1 0
0 1 1 0  0  0 0 1 1
0 1 1 0  1  1 1 0 0
0 1 1 1  0  0 0 1 1
0 1 1 1  1  1 1 1 0
1 0 0 0  0  0 1 0 0
1 0 0 0  1  0 0 0 0
1 0 0 1  0  0 1 0 0
1 0 0 1  1  0 0 1 0
1 0 1 0  0  0 1 0 1
1 0 1 0  1  0 1 0 0
1 0 1 1  0  0 1 0 1
1 0 1 1  1  0 1 1 0
1 1 0 0  0  0 1 1 0
1 1 0 0  1  1 0 0 0
1 1 0 1  0  0 1 1 0
1 1 0 1  1  1 0 1 0
1 1 1 0  0  0 1 1 1
1 1 1 0  1  1 1 0 0
1 1 1 1  0  0 1 1 1
1 1 1 1  1  1 1 1 0
*/
