// Digital circuit original_circuit.dig as structural Verilog
module original_circuit (
  input  x_0,
  input  x_1,
  input  x_2,
  output y_1,
  output y_0
);

  wire and_1_out, not_1_out, not_2_out, not_3_out, not_4_out, or_1_out, or_2_out;

  not not_1 (not_1_out, x_0);
  not not_2 (not_2_out, x_0);
  not not_3 (not_3_out, x_1);
  and and_1 (and_1_out, not_1_out, x_1);
  or or_1 (or_1_out, not_2_out, not_3_out);
  not not_4 (not_4_out, or_1_out);
  or or_2 (or_2_out, and_1_out, not_4_out);
  and and_2 (y_0, or_2_out, x_2);
  not not_5 (y_1, or_2_out);
endmodule
